# Fritzing sketch robot (saved by Fritzing 0.9.3b)

parts:
  Parça1 = Arduino Uno (Rev3)
  M1 = DC Motor
  M2 = DC Motor
  M3 = DC Motor
  M4 = DC Motor
  Parça2 = Bluetooth HC-05 Macho
  S1 = H-Bridge with L298N
  BAT1 = BC9VPC [package=bc9vpc]  # not connected
  BAT2 = Battery Holders [package=lipo-1100mAh]

nets:
  N1: Parça1.D0/RX, Parça2.TXD
  N2: Parça1.D1/TX, Parça2.RXD
  N3: Parça1.D4, S1.IN3
  N4: Parça1.D5_PWM, S1.IN1
  N5: Parça1.D6_PWM, S1.IN2
  N6: Parça1.D7, S1.IN4
  3V3: Parça1.3V3, Parça2.VCC
  GND: Parça1.GND, Parça2.GND
  N7: M1.pin_1, M3.pin_2, S1.M1-02
  N8: M1.pin_2, M3.pin_1, S1.M1-01
  N9: M2.pin_1, M4.pin_2, S1.M2-01
  N10: M2.pin_2, M4.pin_1, S1.M2-02
  N11: S1.12V, BAT2.+
  N12: S1.GND, BAT2.-

custom parts:
  H-Bridge with L298N: h-bridge
